# Fritzing sketch ISHPWiring (saved by Fritzing 0.9.3b)
breadboards: 1

parts:
  Part1 = Adafruit ADXL343 + ADT7410 Sensor FeatherWing [part_number="Adafruit #4147"]
  Part2 = Adafruit 2.13in eInk Under FeatherWing [part_number="Adafruit #4128"]
  Part3 = Adafruit HUZZAH32 ESP32 Feather [part_number="Adafruit #3405"]
  PART1 = SparkFun Soil Moisture Sensor [part_number=SEN-13322]
  KEYPAD1 = Membrane Matrix Keypad  # not connected
  M1 = DC Motor  # not connected
  VCC1 = 4 x AAA Battery Mount  # not connected

nets:
  3.3V: Part1.3.3V, Part2.3.3V, Part3.3.3V, PART1.VCC
  GND: Part1.GND, Part2.GND, Part3.GND, PART1.GND
  N1: Part1.24, Part2.M, Part3.IO12_A11, PART1.SIG

notes:
  Main board on top, EInk on the bottom, real time clock in between. There's also a motor thing between the EInk and the RTC. That should be added. Soon.
  Battery pack connects to a motorshield, which connects to the motor.
  This has a pump on it.

custom parts:
  Adafruit ADXL343 + ADT7410 Sensor FeatherWing: Upgrade any Feather board with motion and precision temperature sensing, with this all-in-one sensing FeatherWing. It sports two fantastic sensors from Analog Devices: an ADXL343 triple-axis accelerometer and an ADT7410 precision temperature sensor. Both sensors are connected over the shared I2C bus, so you can use it with any and all Feathers! We also break out the interrupt pins and address-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
  Adafruit 2.13in eInk Under FeatherWing: Easy e-paper finally comes to your Feather, with this breakout that's designed to make it a breeze to add a tri-color eInk display. Chances are you've seen one of those new-fangled 'e-readers' like the Kindle or Nook. They have gigantic electronic paper 'static' displays - that means the image stays on the display even when power is completely disconnected. The image is also high contrast and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
  SparkFun Soil Moisture Sensor: The SparkFun Soil Moisture Sensor is a simple breakout for measuring the moisture in soil and similar materials.
  Membrane Matrix Keypad: Membrane Matrix 3x4 Keypad
